// Logisim project cpu.circ as structural Verilog: 6 circuits, main circuit main
module main (
  input  [31:0] INSTRUCTION,
  input  CLOCK,
  output [31:0] FETCH_ADDRESS,
  output [31:0] ra_Value,
  output [31:0] sp_Value,
  output [31:0] t0_Value,
  output [31:0] t1_Value,
  output [31:0] t2_Value,
  output [31:0] s0_Value,
  output [31:0] s1_Value,
  output [31:0] a0_Value
);

  wire MEM_p1, MEM_p2, MEM_p4, MEM_p7, MEM_p9, MEM_p11, RegWEn;
  wire [31:0] ALU, multiplexer_1_out, PC__4, RS1, RS2, WB;

  Multiplexer #(.width(32)) multiplexer_1 (.in0(ALU), .in1(PC__4), .out(multiplexer_1_out));  // open: sel, en
  Register #(.width(32)) PC (.D(multiplexer_1_out), .Q(FETCH_ADDRESS), .clk(CLOCK));  // open: en, clr
  Adder #(.width(32)) adder_1 (.a(FETCH_ADDRESS), .b(32'h1), .out(PC__4));  // open: cin, cout
  regfile_main main_1 (
    .Read_Register_1__rs1(INSTRUCTION[19:15]), .Read_Register_2__rs2(INSTRUCTION[24:20]),
    .Write_Register__rd(INSTRUCTION[11:7]), .Write_Data(WB), .Write_Enable(RegWEn), .Clock(CLOCK),
    .Read_Data_1(RS1), .Read_Data_2(RS2), .ra_Value(ra_Value), .sp_Value(sp_Value), .t0_Value(t0_Value),
    .t1_Value(t1_Value), .t2_Value(t2_Value), .s0_Value(s0_Value), .s1_Value(s1_Value), .a0_Value(a0_Value));
  alu_main main_2 (.Switch(4'b0100), .X(32'h4), .Result(ALU), .Y(32'h4));  // open: Equal
  // mem_main MEM: pin names not known; wires that end beside it: MEM_p1, MEM_p2, MEM_p2, MEM_p4, CLOCK, MEM_p4, MEM_p7, MEM_p7, MEM_p9, MEM_p9, MEM_p11

  // Other names for the same wires on the sheet: a0[31:0] = a0_Value; clk = CLOCK; fetch_addr[31:0] = FETCH_ADDRESS;
  //   ra[31:0] = ra_Value; s0[31:0] = s0_Value; s1[31:0] = s1_Value; sp[31:0] = sp_Value; t0[31:0] = t0_Value;
  //   t1[31:0] = t1_Value; t2[31:0] = t2_Value; CONTROL[31:0] = INSTRUCTION; to_IMMGEN[31:0] = INSTRUCTION

  // Notes on the sheet:
  //   Output
  //   These are outputs/inputs from run.circ
  //   Inputs
endmodule

module Control (
  input  [31:0] in_1
);

  wire check_jump_1_select_alu, comparator_1_eq, comparator_2_eq, MemRW, PCSel, RegWEn;
  wire [3:0] op;

  // Probe on in_1[6:0]
  opcode_ID opcode_id_1 (.in_1(in_1[6:0]), .out_2(op));
  // Probe on op
  Multiplexer multiplexer_1 (.in0(1'b1), .in1(1'b0), .out(PCSel), .sel(check_jump_1_select_alu));  // open: en
  check_jump check_jump_1 (.in_1(op), .Select_ALU(check_jump_1_select_alu));
  Multiplexer multiplexer_2 (.in0(1'b1), .in1(1'b0), .out(RegWEn), .sel(comparator_1_eq));  // open: en
  Comparator #(.width(2)) comparator_1 (.a(2'b10), .b(op[2:1]), .eq(comparator_1_eq));  // open: gt, lt
  Multiplexer multiplexer_3 (.in0(1'b0), .in1(1'b1), .out(MemRW), .sel(comparator_2_eq));  // open: en
  Comparator #(.width(4)) comparator_2 (.a(4'b0100), .b(op), .eq(comparator_2_eq));  // open: gt, lt

  // Other names for the same wires on the sheet: funct3[2:0] = in_1[14:12]; funct7[6:0] = in_1[31:25]
endmodule

module opcode_ID (
  input  [6:0] in_1,
  output [3:0] out_2
);

  wire comparator_1_eq, comparator_2_eq, comparator_3_eq, comparator_4_eq, comparator_5_eq, comparator_6_eq,
       comparator_7_eq, comparator_8_eq;
  wire [3:0] multiplexer_1_out, multiplexer_2_out, multiplexer_3_out, multiplexer_4_out, multiplexer_5_out,
       multiplexer_6_out, multiplexer_7_out, multiplexer_8_out;

  Comparator #(.width(7)) comparator_1 (.a(7'b0110011), .b(in_1), .eq(comparator_1_eq));  // open: gt, lt
  Comparator #(.width(7)) comparator_2 (.a(7'b0000011), .b(in_1), .eq(comparator_2_eq));  // open: gt, lt
  Comparator #(.width(7)) comparator_3 (.a(7'b0010011), .b(in_1), .eq(comparator_3_eq));  // open: gt, lt
  Comparator #(.width(7)) comparator_4 (.a(7'b0100011), .b(in_1), .eq(comparator_4_eq));  // open: gt, lt
  Comparator #(.width(7)) comparator_5 (.a(7'b1100011), .b(in_1), .eq(comparator_5_eq));  // open: gt, lt
  Comparator #(.width(7)) comparator_6 (.a(7'b0110111), .b(in_1), .eq(comparator_6_eq));  // open: gt, lt
  Comparator #(.width(7)) comparator_7 (.a(7'b1101111), .b(in_1), .eq(comparator_7_eq));  // open: gt, lt
  Comparator #(.width(7)) comparator_8 (.a(7'b1100111), .b(in_1), .eq(comparator_8_eq));  // open: gt, lt
  Multiplexer #(.width(4)) multiplexer_1 (
    .in0(4'b0000), .in1(4'b0001), .out(multiplexer_1_out), .sel(comparator_1_eq));  // open: en
  Multiplexer #(.width(4)) multiplexer_2 (
    .in0(4'b0000), .in1(4'b0010), .out(multiplexer_2_out), .sel(comparator_2_eq));  // open: en
  Multiplexer #(.width(4)) multiplexer_3 (
    .in0(4'b0000), .in1(4'b0011), .out(multiplexer_3_out), .sel(comparator_3_eq));  // open: en
  Multiplexer #(.width(4)) multiplexer_4 (
    .in0(4'b0000), .in1(4'b0100), .out(multiplexer_4_out), .sel(comparator_4_eq));  // open: en
  Multiplexer #(.width(4)) multiplexer_5 (
    .in0(4'b0000), .in1(4'b0101), .out(multiplexer_5_out), .sel(comparator_5_eq));  // open: en
  Multiplexer #(.width(4)) multiplexer_6 (
    .in0(4'b0000), .in1(4'b0110), .out(multiplexer_6_out), .sel(comparator_6_eq));  // open: en
  Multiplexer #(.width(4)) multiplexer_7 (
    .in0(4'b0000), .in1(4'b0111), .out(multiplexer_7_out), .sel(comparator_7_eq));  // open: en
  Multiplexer #(.width(4)) multiplexer_8 (
    .in0(4'b0000), .in1(4'b1000), .out(multiplexer_8_out), .sel(comparator_8_eq));  // open: en
  assign out_2 = multiplexer_1_out | multiplexer_2_out | multiplexer_3_out | multiplexer_4_out | multiplexer_5_out | multiplexer_6_out | multiplexer_7_out | multiplexer_8_out;  // OR_Gate or_1, 4 bits wide

  // Other names for the same wires on the sheet: opcode[6:0] = in_1

  // Notes on the sheet:
  //   R-type
  //   LOAD
  //   I-type
  //   S-type
  //   SB-type
  //   LUI
  //   JAL
  //   JALR
endmodule

module check_jump (
  input  [3:0] in_1,
  output Select_ALU
);

  wire comparator_1_eq, comparator_2_eq, or_1_out;

  Comparator #(.width(4)) comparator_1 (.a(4'b0111), .b(in_1), .eq(comparator_1_eq));  // open: gt, lt
  Comparator #(.width(4)) comparator_2 (.a(in_1), .b(4'b1000), .eq(comparator_2_eq));  // open: gt, lt
  or or_1 (or_1_out, comparator_1_eq, comparator_2_eq);
  not not_1 (Select_ALU, or_1_out);
endmodule

module check_BSel (
  input  [3:0] in_1
);
endmodule

module ALUSel (
  input  [6:0] OP,
  input  [2:0] FUNCT3,
  input  [6:0] FUNCT7
);

  wire and_1_out, and_2_out, and_3_out, and_4_out, and_5_out, and_6_out, and_7_out, comparator_1_eq,
       comparator_2_eq, comparator_3_eq, comparator_4_eq, comparator_5_eq, comparator_6_eq, comparator_7_eq,
       comparator_8_eq, comparator_9_eq, comparator_10_eq, comparator_11_eq, comparator_12_eq;

  Comparator #(.width(7)) comparator_1 (.a(OP), .b(7'b0110011), .eq(comparator_1_eq));  // open: gt, lt
  Comparator #(.width(3)) comparator_2 (.a(FUNCT3), .b(3'b000), .eq(comparator_2_eq));  // open: gt, lt
  Comparator #(.width(7)) comparator_3 (.a(FUNCT7), .b({7{1'b0}}), .eq(comparator_3_eq));  // open: gt, lt
  Comparator #(.width(7)) comparator_4 (.a(OP), .b(7'b0010011), .eq(comparator_4_eq));  // open: gt, lt
  Comparator #(.width(3)) comparator_5 (.a(FUNCT3), .b(3'b000), .eq(comparator_5_eq));  // open: gt, lt
  Comparator #(.width(7)) comparator_6 (.a(OP), .b(7'b0000011), .eq(comparator_6_eq));  // open: gt, lt
  Comparator #(.width(7)) comparator_7 (.a(OP), .b(7'b0110011), .eq(comparator_7_eq));  // open: gt, lt
  Comparator #(.width(3)) comparator_8 (.a(FUNCT3), .b(3'b000), .eq(comparator_8_eq));  // open: gt, lt
  Comparator #(.width(7)) comparator_9 (.a(OP), .b(7'b1100011), .eq(comparator_9_eq));  // open: gt, lt
  Comparator #(.width(7)) comparator_10 (.a(OP), .b(7'b1101111), .eq(comparator_10_eq));  // open: gt, lt
  Comparator #(.width(7)) comparator_11 (.a(OP), .b(7'b1100111), .eq(comparator_11_eq));  // open: gt, lt
  Comparator #(.width(3)) comparator_12 (.a(FUNCT3), .b(3'b000), .eq(comparator_12_eq));  // open: gt, lt
  and and_1 (and_1_out, comparator_1_eq, comparator_2_eq, comparator_3_eq);
  and and_2 (and_2_out, comparator_4_eq, comparator_5_eq);
  buf and_3 (and_3_out, comparator_6_eq);  // AND_Gate
  and and_4 (and_4_out, comparator_7_eq, comparator_8_eq);
  buf and_5 (and_5_out, comparator_9_eq);  // AND_Gate
  buf and_6 (and_6_out, comparator_10_eq);  // AND_Gate
  and and_7 (and_7_out, comparator_11_eq, comparator_12_eq);
  // OR_Gate or_1 has open pins: in0=and_1_out, in1=and_2_out, in2=and_3_out, in3=and_4_out, in4=and_5_out, in5=and_6_out, in6=and_7_out, out=open

  // Other names for the same wires on the sheet: f3[2:0] = FUNCT3; f7[6:0] = FUNCT7; opcode[6:0] = OP

  // Notes on the sheet:
  //   ADD / R-type
  //   ADD / I-type (not load)
  //   ADD / LOAD
  //   ADD / SW ONLY
  //   ADD / SB
  //   ADD / JAL
  //   ADD / JALR
endmodule
